# Fritzing sketch morse machine v 1,0 (saved by Fritzing 0.9.3b)
breadboards: 1

parts:
  Part1 = Arduino Uno (Rev3)
  LCD1 = LCD screen
  S1 = Pushbutton [package="[THT]"]
  S2 = Pushbutton [package="[THT]"]
  S3 = Pushbutton [package="[THT]"]
  S4 = Pushbutton [package="[THT]"]
  S5 = Pushbutton [package="[THT]"]
  S6 = Pushbutton [package="[THT]"]
  R1 = Trimmer Potentiometer [maximum_resistance=10kΩ package=THT]
  R2 = Trimmer Potentiometer [maximum_resistance=10kΩ package=THT]

nets:
  N1: Part1.D8, S1.Pin_3, S1.Pin_4
  N2: Part1.D9_PWM, S2.Pin_3, S2.Pin_4
  N3: Part1.D10_PWM/SS, S3.Pin_3, S3.Pin_4
  N4: Part1.D11_PWM/MOSI, S4.Pin_3, S4.Pin_4
  N5: Part1.D12/MISO, S5.Pin_3, S5.Pin_4
  N6: Part1.D13/SCK, S6.Pin_3, S6.Pin_4
  N7: Part1.D2, LCD1.RS
  N8: Part1.D3_PWM, LCD1.E
  N9: Part1.D4, LCD1.DB4
  N10: Part1.D5_PWM, LCD1.DB5
  N11: Part1.D6_PWM, LCD1.DB6
  N12: Part1.D7, LCD1.DB7
  5V: Part1.5V, LCD1.VDD, R1.leg1, R2.leg1
  GND: Part1.GND, LCD1.VSS, LCD1.R/W, LCD1.LED-, S1.Pin_1, S1.Pin_2, S2.Pin_1, S2.Pin_2, S3.Pin_1, S3.Pin_2, S4.Pin_1, S4.Pin_2, S5.Pin_1, S5.Pin_2, S6.Pin_1, S6.Pin_2, R1.leg2, R2.leg2
  N13: LCD1.V0, R1.wiper
  N14: LCD1.LED+, R2.wiper
